# Fritzing sketch OnOff (saved by Fritzing 0.9.3b)
perfboards: 1

parts:
  パーツ1 = Arduino Nano (Rev3.0)
  J1 = Basic Servo
  J2 = Basic Servo
  S1 = Pushbutton [package=THT]
  LED1 = RGB LED (com. cathode, rgb) [package="5 mm [THT]"]
  R1 = Resistor [tolerance=±5% resistance=220 package=THT]
  R2 = Resistor [tolerance=±5% resistance=220 package=THT]
  R3 = Resistor [tolerance=±5% resistance=220 package=THT]
  R4 = Resistor [tolerance=±5% resistance=220 package=THT]
  VCC1 = Battery block 9V
  VCC2 = 4 x AAA Battery Mount

nets:
  N1: パーツ1.GND, VCC1.-
  N2: パーツ1.D3, R4.Pin_0
  N3: パーツ1.D5, R3.Pin_0
  N4: パーツ1.D6, R2.Pin_0
  N5: パーツ1.D9, J1.pulse
  N6: パーツ1.D10, J2.pulse
  N7: パーツ1.5V, R1.Pin_0
  GND: J1.gnd, J2.gnd, VCC2.-
  VCC: J1.vcc, J2.vcc, VCC2.+
  N8: S1.leg0, LED1.common_cathode
  N9: S1.leg1, R1.Pin_1
  N10: LED1.red_anode, R4.Pin_1
  N11: LED1.green_anode, R3.Pin_1
  N12: LED1.blue_anode, R2.Pin_1
