# Fritzing sketch OnOff2 (saved by Fritzing 0.9.3b)
perfboards: 1

parts:
  J3 = Basic Servo
  J4 = Basic Servo
  VCC3 = Battery block 9V
  VCC4 = 4 x AAA Battery Mount
  パーツ2 = Arduino Pro Mini v13
  S3 = Pushbutton [package="[THT]"]
  R6 = Resistor [tolerance=±5% resistance=220 package=THT]
  R7 = Resistor [tolerance=±5% resistance=220 package=THT]
  R8 = Resistor [tolerance=±5% resistance=220 package=THT]
  R9 = Resistor [tolerance=±5% resistance=220 package=THT]
  R10 = Resistor [tolerance=±5% resistance=220 package=THT]
  LED2 = RGB LED (com. cathode, rgb) [package="5 mm [THT]"]
  S4 = Pushbutton [package="[THT]"]

nets:
  GND: J3.gnd, J4.gnd, VCC4.-
  VCC: J3.vcc, J4.vcc, VCC4.+
  N1: J3.pulse, パーツ2.D11_PWM/MOSI
  N2: J4.pulse, パーツ2.D10_PWM/SS
  N3: VCC3.-, パーツ2.GND, S3.Pin_3, S3.Pin_4
  N4: VCC3.+, パーツ2.RAW
  N5: パーツ2.RESET, R9.Pin_1
  N6: パーツ2.VCC, R10.Pin_1
  N7: パーツ2.D7, R10.Pin_0, S4.Pin_3, S4.Pin_4
  N8: パーツ2.D6_PWM, R6.Pin_1
  N9: パーツ2.D5_PWM, R7.Pin_1
  N10: パーツ2.D3_PWM, R8.Pin_1
  N11: S3.Pin_1, S3.Pin_2, R9.Pin_0
  N12: R6.Pin_0, LED2.red_anode
  N13: R7.Pin_0, LED2.common_cathode
  N14: R8.Pin_0, LED2.blue_anode
